# Fritzing sketch gps-logger (saved by Fritzing 0.9.4)
breadboards: 1

parts:
  OLED_I2C1 = OLED 128x64 I2C Monochrome Display
  Componente1 = Arduino Mega ADK (Rev3)
  Componente2 = Beitian BN-220 GPS

nets:
  N1: OLED_I2C1.SDA, Componente1.D21/SCL
  N2: OLED_I2C1.SCK, Componente1.D20/SDA
  VDD: OLED_I2C1.VDD, Componente1.5V, Componente2.vcc
  GND: OLED_I2C1.GND, Componente1.GND, Componente2.gnd
  N3: Componente1.D11_PWM, Componente2.tx
  N4: Componente1.D10_PWM, Componente2.rx

custom parts:
  Beitian BN-220 GPS: GPS Module
